# Fritzing sketch flame sensor (saved by Fritzing 0.9.3b)
breadboards: 1

parts:
  J1 = Piezo Speaker  # not connected
  LED1 = smd LED [color="Red (633nm)" package="1206 [SMD]"]
  Part1 = Arduino Uno (Rev3)
  S1 = KY-026
  SG1 = Buzzer 12mm [package=buzzer-ccv-kit]  # not connected
  J2 = Piezo Speaker  # not connected
  J3 = Piezo Speaker  # not connected
  J4 = Piezo Speaker  # not connected
  J5 = Piezo Speaker  # not connected
  J6 = Piezo Speaker  # not connected
  SG2 = Buzzer 12mm [part_number=COM-07950 package=buzzer-12mm-ns]
  R1 = Resistor [tolerance=±5% resistance=220 package=THT]

nets:
  N1: LED1.cathode, Part1.D7
  N2: LED1.anode, R1.Pin_1
  N3: Part1.D12/MISO, SG2.1
  N4: Part1.GND, S1.pin2, SG2.2, R1.Pin_0
  N5: Part1.D2, S1.pin4
  N6: Part1.5V, S1.pin3

custom parts:
  KY-026: ky-026 flame sensor module
  Buzzer 12mm: Buzzer 12mm Spark Fun Electronics SKU : Comp-Buzzer Through hole This is a small 12mm round speaker that operates around the audible 2kHz range. You can use these speakers to create simple music or user interfaces. This is not a true piezoelectric speaker but behaves similarly. Instead of a piezoelectric crystal that vibrates with an electric current, this tiny speaker uses an electromagnet to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

// code stored in the sketch: flame sensor.ino
int sensorPin = 2; 

int sensorValue; 

int led = 7; 

int buzzer = 12; 

void setup() {


pinMode(led, OUTPUT);

pinMode(buzzer,OUTPUT);

pinMode(sensorPin, INPUT);

}

void loop()

{


sensorValue = digitalRead(sensorPin);


if (sensorValue == HIGH)

{

digitalWrite(led,HIGH);

digitalWrite(buzzer,HIGH);

delay(1000);

} 

else{

digitalWrite(led,LOW);

digitalWrite(buzzer,LOW);

}

}
